# Fritzing sketch herald (saved by Fritzing 0.9.6b)
breadboards: 1

parts:
  M1 = fc-51 [package=THT]
  B1 = Bolt WiFi Module [package=dip]

nets:
  N1: M1.pin1, B1.pin7
  N2: M1.pin2, B1.pin1
  N3: M1.pin3, B1.pin11

custom parts:
  Bolt WiFi Module: Bolt IoT platform gives you the capability to control your devices and collect data from IoT devices safely and securely no matter where you are. Get actionable insights by deploying machine learning algorithms with just a few clicks to detect anomalies as well as predict sensor values.
